# Fritzing sketch sigfox-oximeter-proto (saved by Fritzing 0.9.3b)
breadboards: 1

parts:
  M1 = MAX30102
  VCC1 = Battery
  OLED1 = OLED 128x64 I2C Monochrome Display
  MKRFox1 = Arduino MKR Fox 1200

nets:
  VIN: M1.VIN, OLED1.VDD, MKRFox1.DAC/A0, MKRFox1.VCC
  N1: M1.SCL, OLED1.SCK, MKRFox1.12/SCL
  N2: M1.SDA, OLED1.SDA, MKRFox1.11/SDA
  N3: M1.INT, MKRFox1.10/MISO
  GND: M1.GND, VCC1.-, OLED1.GND, MKRFox1.GND
  N4: VCC1.+, MKRFox1.VIN

custom parts:
  MAX30102: Oximeter module using the MAX30102 chip. You may wish to read (and check your module) this post on power problems with these modules: https://reedpaper.wordpress.com/2018/08/22/pulse-oximeter-max30100-max30102-how-to-fix-wrong-board/ . As usual, if you want the mounting holes in pcb, you need to drag a hole over the pad in silkscreen to actually drill the hole (by default they are not drilled)
